// Logisim project ENCODER3TO8.circ as structural Verilog: 6 circuits, main circuit main
module main (
  input  E,
  input  A2,
  input  A1,
  input  A0,
  output Z7,
  output Z6,
  output Z5,
  output Z4,
  output Z3,
  output Z2,
  output Z1,
  output Z0
);

  wire not_1_out, not_2_out, not_3_out;

  not not_1 (not_1_out, A2);
  not not_2 (not_2_out, A1);
  not not_3 (not_3_out, A0);
  and and_1 (Z7, A0, A1, A2, E);
  and and_2 (Z6, A2, A1, not_3_out, E);
  and and_3 (Z5, A2, not_2_out, A0, E);
  and and_4 (Z4, A2, not_2_out, not_3_out, E);
  and and_5 (Z3, not_1_out, A1, A0, E);
  and and_6 (Z2, not_1_out, A1, not_3_out, E);
  and and_7 (Z1, not_1_out, not_2_out, A0, E);
  and and_8 (Z0, not_1_out, not_2_out, not_3_out, E);
endmodule

module _4_16 (
  input  in_1,
  input  in_2,
  input  in_3,
  input  in_4,
  output z_15,
  output z_14,
  output z_13,
  output z_12,
  output z_11,
  output z_10,
  output z_9,
  output z_8,
  output z_7,
  output z_6,
  output z_5,
  output z_4,
  output z_3,
  output z_2,
  output z_1,
  output z_0
);

  wire not_1_out;

  not not_1 (not_1_out, in_1);
  main main_1 (
    .E(in_1), .A2(in_2), .A1(in_3), .A0(in_4), .Z7(z_15), .Z6(z_14), .Z5(z_13), .Z4(z_12), .Z3(z_11),
    .Z2(z_10), .Z1(z_9), .Z0(z_8));
  main main_2 (
    .E(not_1_out), .A2(in_2), .A1(in_3), .A0(in_4), .Z7(z_7), .Z6(z_6), .Z5(z_5), .Z4(z_4), .Z3(z_3),
    .Z2(z_2), .Z1(z_1), .Z0(z_0));
endmodule

module bcd_e_3 (
  input  in_1,
  input  in_2,
  input  in_3,
  input  in_4,
  output out_5,
  output out_6,
  output out_7,
  output out_8
);

  wire n4_16_1_z_0, n4_16_1_z_1, n4_16_1_z_2, n4_16_1_z_3, n4_16_1_z_4, n4_16_1_z_5, n4_16_1_z_6,
       n4_16_1_z_7, n4_16_1_z_8, n4_16_1_z_9;

  _4_16 u_4_16_1 (
    .in_1(in_1), .in_2(in_2), .in_3(in_3), .in_4(in_4), .z_9(n4_16_1_z_9), .z_8(n4_16_1_z_8),
    .z_7(n4_16_1_z_7), .z_6(n4_16_1_z_6), .z_5(n4_16_1_z_5), .z_4(n4_16_1_z_4), .z_3(n4_16_1_z_3),
    .z_2(n4_16_1_z_2), .z_1(n4_16_1_z_1), .z_0(n4_16_1_z_0));  // open: z_15, z_14, z_13, z_12, z_11, z_10
  or w (out_5, n4_16_1_z_9, n4_16_1_z_8, n4_16_1_z_7, n4_16_1_z_6, n4_16_1_z_5);
  or x (out_6, n4_16_1_z_9, n4_16_1_z_4, n4_16_1_z_3, n4_16_1_z_2, n4_16_1_z_1);
  or y (out_7, n4_16_1_z_7, n4_16_1_z_8, n4_16_1_z_4, n4_16_1_z_3, n4_16_1_z_0);
  or z (out_8, n4_16_1_z_0, n4_16_1_z_2, n4_16_1_z_4, n4_16_1_z_6, n4_16_1_z_8);
endmodule

module mult (
  input  K0,
  input  K1,
  input  K2,
  input  K3,
  input  S1,
  input  S0,
  output L
);

  wire and_1_out, and_2_out, and_3_out, and_4_out, not_1_out, not_2_out;

  not not_1 (not_1_out, S1);
  not not_2 (not_2_out, S0);
  and and_1 (and_1_out, K0, not_1_out, not_2_out);
  and and_2 (and_2_out, K1, not_1_out, S0);
  and and_3 (and_3_out, K2, S1, not_2_out);
  and and_4 (and_4_out, K3, S1, S0);
  or or_1 (L, and_1_out, and_2_out, and_3_out, and_4_out);
endmodule

module _4to4mult (
  input  [3:0] in_1,
  input  [3:0] in_2,
  input  [3:0] in_3,
  input  [3:0] in_4,
  input  [1:0] in_5,
  output [3:0] out_6
);

  mult mult_1 (.K0(in_4[0]), .K1(in_3[0]), .K2(in_2[0]), .K3(in_1[0]), .S1(in_5[1]), .S0(in_5[0]), .L(out_6[0]));
  mult mult_2 (.K0(in_4[1]), .K1(in_3[1]), .K2(in_2[1]), .K3(in_1[1]), .S1(in_5[1]), .S0(in_5[0]), .L(out_6[1]));
  mult mult_3 (.K0(in_4[2]), .K1(in_3[2]), .K2(in_2[2]), .K3(in_1[2]), .S1(in_5[1]), .S0(in_5[0]), .L(out_6[2]));
  mult mult_4 (.K0(in_4[3]), .K1(in_3[3]), .K2(in_2[3]), .K3(in_1[3]), .S1(in_5[1]), .S0(in_5[0]), .L(out_6[3]));
endmodule

module control (
  input  [3:0] in_1,
  input  [1:0] in_2
);

  wire [3:0] bcd_e_3_1_out_5, multiplexer_1_out, not_1_out, or_1_out;

  bcd_e_3 bcd_e_3_1 (
    .in_1(in_1[0]), .in_2(in_1[1]), .in_3(in_1[2]), .in_4(in_1[3]), .out_5(bcd_e_3_1_out_5[0]),
    .out_6(bcd_e_3_1_out_5[1]), .out_7(bcd_e_3_1_out_5[2]), .out_8(bcd_e_3_1_out_5[3]));
  assign or_1_out = in_1 | bcd_e_3_1_out_5;  // OR_Gate or_1, 4 bits wide
  assign not_1_out = ~in_1;  // NOT_Gate not_1, 4 bits wide
  Hex_Digit_Display hex_digit_display_1 (.value(multiplexer_1_out));  // open: dp
  Multiplexer #(.select(2), .width(4)) multiplexer_1 (
    .in0(in_1), .in1(not_1_out), .in2(or_1_out), .in3(bcd_e_3_1_out_5), .out(multiplexer_1_out), .sel(in_2));  // open: en
endmodule
